# Fritzing sketch Untitled Sketch 2 (saved by Fritzing 0.9.3b)
breadboards: 1

parts:
  Componente1 = Arduino Mega ADK (Rev3)
  PIR1 = PIR sensor
  S1 = H-Bridge with L298N
  M3 = DC Motor  # not connected
  M4 = DC Motor

nets:
  N1: Componente1.D11_PWM, S1.IN1
  N2: Componente1.D10_PWM, S1.IN2
  N3: Componente1.D9_PWM, S1.IN3
  N4: Componente1.D8_PWM, S1.IN4
  5V: Componente1.5V, PIR1.VDD, S1.5V
  GND: Componente1.GND, PIR1.GND, S1.GND
  N5: Componente1.D4_PWM, PIR1.SIG
  N6: S1.OUT4-Motor2, M4.pin_1

custom parts:
  H-Bridge with L298N: h-bridge
